// Logisim project main.circ as structural Verilog: 9 circuits, main circuit main
module main (
);

  wire _0_clk, _1_clk, _2_clk, _3_clk, _4_clk, _5_clk, _6_clk, _7_clk, clk, controller_1_irq, down, flag,
       left, open, reset, right, up;
  wire [2:0] controller_1_vec;
  wire [6:0] row_drawer_1__00, row_drawer_1__01, row_drawer_1__02, row_drawer_1__03, row_drawer_1__04,
       row_drawer_1__05, row_drawer_1__06, row_drawer_1__07, row_drawer_1__10, row_drawer_1__11,
       row_drawer_1__12, row_drawer_1__13, row_drawer_1__14, row_drawer_1__15, row_drawer_1__16,
       row_drawer_1__17, row_drawer_1__20, row_drawer_1__21, row_drawer_1__22, row_drawer_1__23,
       row_drawer_1__24, row_drawer_1__25, row_drawer_1__26, row_drawer_1__27, row_drawer_1__30,
       row_drawer_1__31, row_drawer_1__32, row_drawer_1__33, row_drawer_1__34, row_drawer_1__35,
       row_drawer_1__36, row_drawer_1__37, row_drawer_1__40, row_drawer_1__41, row_drawer_1__42,
       row_drawer_1__43, row_drawer_1__44, row_drawer_1__45, row_drawer_1__46, row_drawer_1__47,
       row_drawer_1__50, row_drawer_1__51, row_drawer_1__52, row_drawer_1__53, row_drawer_1__54,
       row_drawer_1__55, row_drawer_1__56, row_drawer_1__57, row_drawer_1__60, row_drawer_1__61,
       row_drawer_1__62, row_drawer_1__63, row_drawer_1__64, row_drawer_1__65, row_drawer_1__66,
       row_drawer_1__67, row_drawer_1__70, row_drawer_1__71, row_drawer_1__72, row_drawer_1__73,
       row_drawer_1__74, row_drawer_1__75, row_drawer_1__76, row_drawer_1__77, row_drawer_2__00,
       row_drawer_2__01, row_drawer_2__02, row_drawer_2__03, row_drawer_2__04, row_drawer_2__05,
       row_drawer_2__06, row_drawer_2__07, row_drawer_2__10, row_drawer_2__11, row_drawer_2__12,
       row_drawer_2__13, row_drawer_2__14, row_drawer_2__15, row_drawer_2__16, row_drawer_2__17,
       row_drawer_2__20, row_drawer_2__21, row_drawer_2__22, row_drawer_2__23, row_drawer_2__24,
       row_drawer_2__25, row_drawer_2__26, row_drawer_2__27, row_drawer_2__30, row_drawer_2__31,
       row_drawer_2__32, row_drawer_2__33, row_drawer_2__34, row_drawer_2__35, row_drawer_2__36,
       row_drawer_2__37, row_drawer_2__40, row_drawer_2__41, row_drawer_2__42, row_drawer_2__43,
       row_drawer_2__44, row_drawer_2__45, row_drawer_2__46, row_drawer_2__47, row_drawer_2__50,
       row_drawer_2__51, row_drawer_2__52, row_drawer_2__53, row_drawer_2__54, row_drawer_2__55,
       row_drawer_2__56, row_drawer_2__57, row_drawer_2__60, row_drawer_2__61, row_drawer_2__62,
       row_drawer_2__63, row_drawer_2__64, row_drawer_2__65, row_drawer_2__66, row_drawer_2__67,
       row_drawer_2__70, row_drawer_2__71, row_drawer_2__72, row_drawer_2__73, row_drawer_2__74,
       row_drawer_2__75, row_drawer_2__76, row_drawer_2__77, row_drawer_3__00, row_drawer_3__01,
       row_drawer_3__02, row_drawer_3__03, row_drawer_3__04, row_drawer_3__05, row_drawer_3__06,
       row_drawer_3__07, row_drawer_3__10, row_drawer_3__11, row_drawer_3__12, row_drawer_3__13,
       row_drawer_3__14, row_drawer_3__15, row_drawer_3__16, row_drawer_3__17, row_drawer_3__20,
       row_drawer_3__21, row_drawer_3__22, row_drawer_3__23, row_drawer_3__24, row_drawer_3__25,
       row_drawer_3__26, row_drawer_3__27, row_drawer_3__30, row_drawer_3__31, row_drawer_3__32,
       row_drawer_3__33, row_drawer_3__34, row_drawer_3__35, row_drawer_3__36, row_drawer_3__37,
       row_drawer_3__40, row_drawer_3__41, row_drawer_3__42, row_drawer_3__43, row_drawer_3__44,
       row_drawer_3__45, row_drawer_3__46, row_drawer_3__47, row_drawer_3__50, row_drawer_3__51,
       row_drawer_3__52, row_drawer_3__53, row_drawer_3__54, row_drawer_3__55, row_drawer_3__56,
       row_drawer_3__57, row_drawer_3__60, row_drawer_3__61, row_drawer_3__62, row_drawer_3__63,
       row_drawer_3__64, row_drawer_3__65, row_drawer_3__66, row_drawer_3__67, row_drawer_3__70,
       row_drawer_3__71, row_drawer_3__72, row_drawer_3__73, row_drawer_3__74, row_drawer_3__75,
       row_drawer_3__76, row_drawer_3__77, row_drawer_4__00, row_drawer_4__01, row_drawer_4__02,
       row_drawer_4__03, row_drawer_4__04, row_drawer_4__05, row_drawer_4__06, row_drawer_4__07,
       row_drawer_4__10, row_drawer_4__11, row_drawer_4__12, row_drawer_4__13, row_drawer_4__14,
       row_drawer_4__15, row_drawer_4__16, row_drawer_4__17, row_drawer_4__20, row_drawer_4__21,
       row_drawer_4__22, row_drawer_4__23, row_drawer_4__24, row_drawer_4__25, row_drawer_4__26,
       row_drawer_4__27, row_drawer_4__30, row_drawer_4__31, row_drawer_4__32, row_drawer_4__33,
       row_drawer_4__34, row_drawer_4__35, row_drawer_4__36, row_drawer_4__37, row_drawer_4__40,
       row_drawer_4__41, row_drawer_4__42, row_drawer_4__43, row_drawer_4__44, row_drawer_4__45,
       row_drawer_4__46, row_drawer_4__47, row_drawer_4__50, row_drawer_4__51, row_drawer_4__52,
       row_drawer_4__53, row_drawer_4__54, row_drawer_4__55, row_drawer_4__56, row_drawer_4__57,
       row_drawer_4__60, row_drawer_4__61, row_drawer_4__62, row_drawer_4__63, row_drawer_4__64,
       row_drawer_4__65, row_drawer_4__66, row_drawer_4__67, row_drawer_4__70, row_drawer_4__71,
       row_drawer_4__72, row_drawer_4__73, row_drawer_4__74, row_drawer_4__75, row_drawer_4__76,
       row_drawer_4__77, row_drawer_5_p3, row_drawer_5_p4, row_drawer_5_p5, row_drawer_5_p6, row_drawer_5_p7,
       row_drawer_5_p8, row_drawer_5_p9, row_drawer_5_p10, row_drawer_5_p11, row_drawer_5_p12,
       row_drawer_5_p13, row_drawer_5_p14, row_drawer_5_p15, row_drawer_5_p16, row_drawer_5_p17,
       row_drawer_5_p18, row_drawer_5_p19, row_drawer_5_p20, row_drawer_5_p21, row_drawer_5_p22,
       row_drawer_5_p23, row_drawer_5_p24, row_drawer_5_p25, row_drawer_5_p26, row_drawer_5_p27,
       row_drawer_5_p28, row_drawer_5_p29, row_drawer_5_p30, row_drawer_5_p31, row_drawer_5_p32,
       row_drawer_5_p33, row_drawer_5_p34, row_drawer_5_p35, row_drawer_5_p36, row_drawer_5_p37,
       row_drawer_5_p38, row_drawer_5_p39, row_drawer_5_p40, row_drawer_5_p41, row_drawer_5_p42,
       row_drawer_5_p43, row_drawer_5_p44, row_drawer_5_p45, row_drawer_5_p46, row_drawer_5_p47,
       row_drawer_5_p48, row_drawer_5_p49, row_drawer_5_p50, row_drawer_5_p51, row_drawer_5_p52,
       row_drawer_5_p53, row_drawer_5_p54, row_drawer_5_p55, row_drawer_5_p56, row_drawer_5_p57,
       row_drawer_5_p58, row_drawer_5_p59, row_drawer_5_p60, row_drawer_5_p61, row_drawer_5_p62,
       row_drawer_5_p63, row_drawer_5_p64, row_drawer_5_p65, row_drawer_5_p66, row_drawer_6__00,
       row_drawer_6__01, row_drawer_6__02, row_drawer_6__03, row_drawer_6__04, row_drawer_6__05,
       row_drawer_6__06, row_drawer_6__07, row_drawer_6__10, row_drawer_6__11, row_drawer_6__12,
       row_drawer_6__13, row_drawer_6__14, row_drawer_6__15, row_drawer_6__16, row_drawer_6__17,
       row_drawer_6__20, row_drawer_6__21, row_drawer_6__22, row_drawer_6__23, row_drawer_6__24,
       row_drawer_6__25, row_drawer_6__26, row_drawer_6__27, row_drawer_6__30, row_drawer_6__31,
       row_drawer_6__32, row_drawer_6__33, row_drawer_6__34, row_drawer_6__35, row_drawer_6__36,
       row_drawer_6__37, row_drawer_6__40, row_drawer_6__41, row_drawer_6__42, row_drawer_6__43,
       row_drawer_6__44, row_drawer_6__45, row_drawer_6__46, row_drawer_6__47, row_drawer_6__50,
       row_drawer_6__51, row_drawer_6__52, row_drawer_6__53, row_drawer_6__54, row_drawer_6__55,
       row_drawer_6__56, row_drawer_6__57, row_drawer_6__60, row_drawer_6__61, row_drawer_6__62,
       row_drawer_6__63, row_drawer_6__64, row_drawer_6__65, row_drawer_6__66, row_drawer_6__67,
       row_drawer_6__70, row_drawer_6__71, row_drawer_6__72, row_drawer_6__73, row_drawer_6__74,
       row_drawer_6__75, row_drawer_6__76, row_drawer_6__77, row_drawer_7__00, row_drawer_7__01,
       row_drawer_7__02, row_drawer_7__03, row_drawer_7__04, row_drawer_7__05, row_drawer_7__06,
       row_drawer_7__07, row_drawer_7__10, row_drawer_7__11, row_drawer_7__12, row_drawer_7__13,
       row_drawer_7__14, row_drawer_7__15, row_drawer_7__16, row_drawer_7__17, row_drawer_7__20,
       row_drawer_7__21, row_drawer_7__22, row_drawer_7__23, row_drawer_7__24, row_drawer_7__25,
       row_drawer_7__26, row_drawer_7__27, row_drawer_7__30, row_drawer_7__31, row_drawer_7__32,
       row_drawer_7__33, row_drawer_7__34, row_drawer_7__35, row_drawer_7__36, row_drawer_7__37,
       row_drawer_7__40, row_drawer_7__41, row_drawer_7__42, row_drawer_7__43, row_drawer_7__44,
       row_drawer_7__45, row_drawer_7__46, row_drawer_7__47, row_drawer_7__50, row_drawer_7__51,
       row_drawer_7__52, row_drawer_7__53, row_drawer_7__54, row_drawer_7__55, row_drawer_7__56,
       row_drawer_7__57, row_drawer_7__60, row_drawer_7__61, row_drawer_7__62, row_drawer_7__63,
       row_drawer_7__64, row_drawer_7__65, row_drawer_7__66, row_drawer_7__67, row_drawer_7__70,
       row_drawer_7__71, row_drawer_7__72, row_drawer_7__73, row_drawer_7__74, row_drawer_7__75,
       row_drawer_7__76, row_drawer_7__77, row_drawer_8__00, row_drawer_8__01, row_drawer_8__02,
       row_drawer_8__03, row_drawer_8__04, row_drawer_8__05, row_drawer_8__06, row_drawer_8__07,
       row_drawer_8__10, row_drawer_8__11, row_drawer_8__12, row_drawer_8__13, row_drawer_8__14,
       row_drawer_8__15, row_drawer_8__16, row_drawer_8__17, row_drawer_8__20, row_drawer_8__21,
       row_drawer_8__22, row_drawer_8__23, row_drawer_8__24, row_drawer_8__25, row_drawer_8__26,
       row_drawer_8__27, row_drawer_8__30, row_drawer_8__31, row_drawer_8__32, row_drawer_8__33,
       row_drawer_8__34, row_drawer_8__35, row_drawer_8__36, row_drawer_8__37, row_drawer_8__40,
       row_drawer_8__41, row_drawer_8__42, row_drawer_8__43, row_drawer_8__44, row_drawer_8__45,
       row_drawer_8__46, row_drawer_8__47, row_drawer_8__50, row_drawer_8__51, row_drawer_8__52,
       row_drawer_8__53, row_drawer_8__54, row_drawer_8__55, row_drawer_8__56, row_drawer_8__57,
       row_drawer_8__60, row_drawer_8__61, row_drawer_8__62, row_drawer_8__63, row_drawer_8__64,
       row_drawer_8__65, row_drawer_8__66, row_drawer_8__67, row_drawer_8__70, row_drawer_8__71,
       row_drawer_8__72, row_drawer_8__73, row_drawer_8__74, row_drawer_8__75, row_drawer_8__76,
       row_drawer_8__77;
  wire [31:0] _0_row_data, _1_row_data, _2_row_data, _3_left, _4_row_data, _5_row_data, _6_row_data, _7_left;

  Button button (.out(up));
  Button button_2 (.out(left));
  Button v (.out(down));
  Button R (.out(reset));
  Button F (.out(flag));
  Button button_3 (.out(right));
  Button O (.out(open));
  row_drawer row_drawer_1 (
    ._00(row_drawer_1__00), ._01(row_drawer_1__01), ._02(row_drawer_1__02), ._03(row_drawer_1__03),
    ._04(row_drawer_1__04), ._05(row_drawer_1__05), ._06(row_drawer_1__06), ._07(row_drawer_1__07),
    ._10(row_drawer_1__10), ._11(row_drawer_1__11), ._12(row_drawer_1__12), ._13(row_drawer_1__13),
    ._14(row_drawer_1__14), ._15(row_drawer_1__15), ._16(row_drawer_1__16), ._17(row_drawer_1__17),
    ._20(row_drawer_1__20), ._21(row_drawer_1__21), ._22(row_drawer_1__22), ._23(row_drawer_1__23),
    ._24(row_drawer_1__24), ._25(row_drawer_1__25), ._26(row_drawer_1__26), ._27(row_drawer_1__27),
    ._30(row_drawer_1__30), ._31(row_drawer_1__31), ._32(row_drawer_1__32), ._33(row_drawer_1__33),
    ._34(row_drawer_1__34), ._35(row_drawer_1__35), ._36(row_drawer_1__36), ._37(row_drawer_1__37),
    ._60(row_drawer_1__60), ._61(row_drawer_1__61), ._62(row_drawer_1__62), ._63(row_drawer_1__63),
    ._64(row_drawer_1__64), ._65(row_drawer_1__65), ._66(row_drawer_1__66), ._67(row_drawer_1__67),
    ._70(row_drawer_1__70), ._40(row_drawer_1__40), ._71(row_drawer_1__71), ._41(row_drawer_1__41),
    ._72(row_drawer_1__72), ._42(row_drawer_1__42), ._73(row_drawer_1__73), ._43(row_drawer_1__43),
    ._74(row_drawer_1__74), ._44(row_drawer_1__44), ._75(row_drawer_1__75), ._45(row_drawer_1__45),
    ._76(row_drawer_1__76), ._46(row_drawer_1__46), ._77(row_drawer_1__77), ._47(row_drawer_1__47),
    ._50(row_drawer_1__50), ._51(row_drawer_1__51), ._52(row_drawer_1__52), ._53(row_drawer_1__53),
    ._54(row_drawer_1__54), ._55(row_drawer_1__55), ._56(row_drawer_1__56), ._57(row_drawer_1__57),
    .clk(_0_clk), .data(_0_row_data));  // open: left, right
  DotMatrix #(.matrixcols(8)) dotmatrix_1 (
    .col0(row_drawer_1__00), .col1(row_drawer_1__01), .col2(row_drawer_1__02), .col3(row_drawer_1__03),
    .col4(row_drawer_1__04), .col5(row_drawer_1__05), .col6(row_drawer_1__06), .col7(row_drawer_1__07));
  DotMatrix #(.matrixcols(8)) dotmatrix_2 (
    .col0(row_drawer_2__00), .col1(row_drawer_2__01), .col2(row_drawer_2__02), .col3(row_drawer_2__03),
    .col4(row_drawer_2__04), .col5(row_drawer_2__05), .col6(row_drawer_2__06), .col7(row_drawer_2__07));
  row_drawer row_drawer_2 (
    ._00(row_drawer_2__00), ._01(row_drawer_2__01), ._02(row_drawer_2__02), ._03(row_drawer_2__03),
    ._04(row_drawer_2__04), ._05(row_drawer_2__05), ._06(row_drawer_2__06), ._07(row_drawer_2__07),
    ._10(row_drawer_2__10), ._11(row_drawer_2__11), ._12(row_drawer_2__12), ._13(row_drawer_2__13),
    ._14(row_drawer_2__14), ._15(row_drawer_2__15), ._16(row_drawer_2__16), ._17(row_drawer_2__17),
    ._20(row_drawer_2__20), ._21(row_drawer_2__21), ._22(row_drawer_2__22), ._23(row_drawer_2__23),
    ._24(row_drawer_2__24), ._25(row_drawer_2__25), ._26(row_drawer_2__26), ._27(row_drawer_2__27),
    ._30(row_drawer_2__30), ._31(row_drawer_2__31), ._32(row_drawer_2__32), ._33(row_drawer_2__33),
    ._34(row_drawer_2__34), ._35(row_drawer_2__35), ._36(row_drawer_2__36), ._37(row_drawer_2__37),
    ._60(row_drawer_2__60), ._61(row_drawer_2__61), ._62(row_drawer_2__62), ._63(row_drawer_2__63),
    ._64(row_drawer_2__64), ._65(row_drawer_2__65), ._66(row_drawer_2__66), ._67(row_drawer_2__67),
    ._70(row_drawer_2__70), ._40(row_drawer_2__40), ._71(row_drawer_2__71), ._41(row_drawer_2__41),
    ._72(row_drawer_2__72), ._42(row_drawer_2__42), ._73(row_drawer_2__73), ._43(row_drawer_2__43),
    ._74(row_drawer_2__74), ._44(row_drawer_2__44), ._75(row_drawer_2__75), ._45(row_drawer_2__45),
    ._76(row_drawer_2__76), ._46(row_drawer_2__46), ._77(row_drawer_2__77), ._47(row_drawer_2__47),
    ._50(row_drawer_2__50), ._51(row_drawer_2__51), ._52(row_drawer_2__52), ._53(row_drawer_2__53),
    ._54(row_drawer_2__54), ._55(row_drawer_2__55), ._56(row_drawer_2__56), ._57(row_drawer_2__57),
    .clk(_1_clk), .data(_1_row_data));  // open: left, right
  row_drawer row_drawer_3 (
    ._00(row_drawer_3__00), ._01(row_drawer_3__01), ._02(row_drawer_3__02), ._03(row_drawer_3__03),
    ._04(row_drawer_3__04), ._05(row_drawer_3__05), ._06(row_drawer_3__06), ._07(row_drawer_3__07),
    ._10(row_drawer_3__10), ._11(row_drawer_3__11), ._12(row_drawer_3__12), ._13(row_drawer_3__13),
    ._14(row_drawer_3__14), ._15(row_drawer_3__15), ._16(row_drawer_3__16), ._17(row_drawer_3__17),
    ._20(row_drawer_3__20), ._21(row_drawer_3__21), ._22(row_drawer_3__22), ._23(row_drawer_3__23),
    ._24(row_drawer_3__24), ._25(row_drawer_3__25), ._26(row_drawer_3__26), ._27(row_drawer_3__27),
    ._30(row_drawer_3__30), ._31(row_drawer_3__31), ._32(row_drawer_3__32), ._33(row_drawer_3__33),
    ._34(row_drawer_3__34), ._35(row_drawer_3__35), ._36(row_drawer_3__36), ._37(row_drawer_3__37),
    ._60(row_drawer_3__60), ._61(row_drawer_3__61), ._62(row_drawer_3__62), ._63(row_drawer_3__63),
    ._64(row_drawer_3__64), ._65(row_drawer_3__65), ._66(row_drawer_3__66), ._67(row_drawer_3__67),
    ._70(row_drawer_3__70), ._40(row_drawer_3__40), ._71(row_drawer_3__71), ._41(row_drawer_3__41),
    ._72(row_drawer_3__72), ._42(row_drawer_3__42), ._73(row_drawer_3__73), ._43(row_drawer_3__43),
    ._74(row_drawer_3__74), ._44(row_drawer_3__44), ._75(row_drawer_3__75), ._45(row_drawer_3__45),
    ._76(row_drawer_3__76), ._46(row_drawer_3__46), ._77(row_drawer_3__77), ._47(row_drawer_3__47),
    ._50(row_drawer_3__50), ._51(row_drawer_3__51), ._52(row_drawer_3__52), ._53(row_drawer_3__53),
    ._54(row_drawer_3__54), ._55(row_drawer_3__55), ._56(row_drawer_3__56), ._57(row_drawer_3__57),
    .clk(_2_clk), .data(_2_row_data));  // open: left, right
  DotMatrix #(.matrixcols(8)) dotmatrix_3 (
    .col0(row_drawer_3__00), .col1(row_drawer_3__01), .col2(row_drawer_3__02), .col3(row_drawer_3__03),
    .col4(row_drawer_3__04), .col5(row_drawer_3__05), .col6(row_drawer_3__06), .col7(row_drawer_3__07));
  DotMatrix #(.matrixcols(8)) dotmatrix_4 (
    .col0(row_drawer_4__00), .col1(row_drawer_4__01), .col2(row_drawer_4__02), .col3(row_drawer_4__03),
    .col4(row_drawer_4__04), .col5(row_drawer_4__05), .col6(row_drawer_4__06), .col7(row_drawer_4__07));
  row_drawer row_drawer_4 (
    ._00(row_drawer_4__00), ._01(row_drawer_4__01), ._02(row_drawer_4__02), ._03(row_drawer_4__03),
    ._04(row_drawer_4__04), ._05(row_drawer_4__05), ._06(row_drawer_4__06), ._07(row_drawer_4__07),
    ._10(row_drawer_4__10), ._11(row_drawer_4__11), ._12(row_drawer_4__12), ._13(row_drawer_4__13),
    ._14(row_drawer_4__14), ._15(row_drawer_4__15), ._16(row_drawer_4__16), ._17(row_drawer_4__17),
    ._20(row_drawer_4__20), ._21(row_drawer_4__21), ._22(row_drawer_4__22), ._23(row_drawer_4__23),
    ._24(row_drawer_4__24), ._25(row_drawer_4__25), ._26(row_drawer_4__26), ._27(row_drawer_4__27),
    ._30(row_drawer_4__30), ._31(row_drawer_4__31), ._32(row_drawer_4__32), ._33(row_drawer_4__33),
    ._34(row_drawer_4__34), ._35(row_drawer_4__35), ._36(row_drawer_4__36), ._37(row_drawer_4__37),
    ._60(row_drawer_4__60), ._61(row_drawer_4__61), ._62(row_drawer_4__62), ._63(row_drawer_4__63),
    ._64(row_drawer_4__64), ._65(row_drawer_4__65), ._66(row_drawer_4__66), ._67(row_drawer_4__67),
    ._70(row_drawer_4__70), ._40(row_drawer_4__40), ._71(row_drawer_4__71), ._41(row_drawer_4__41),
    ._72(row_drawer_4__72), ._42(row_drawer_4__42), ._73(row_drawer_4__73), ._43(row_drawer_4__43),
    ._74(row_drawer_4__74), ._44(row_drawer_4__44), ._75(row_drawer_4__75), ._45(row_drawer_4__45),
    ._76(row_drawer_4__76), ._46(row_drawer_4__46), ._77(row_drawer_4__77), ._47(row_drawer_4__47),
    ._50(row_drawer_4__50), ._51(row_drawer_4__51), ._52(row_drawer_4__52), ._53(row_drawer_4__53),
    ._54(row_drawer_4__54), ._55(row_drawer_4__55), ._56(row_drawer_4__56), ._57(row_drawer_4__57),
    .clk(_3_clk), .data(_3_left));  // open: left, right
  // row_drawer row_drawer_5: pin names not known; wires that end beside it: _4_clk, _4_row_data, row_drawer_5_p3, row_drawer_5_p4, row_drawer_5_p5, row_drawer_5_p6, row_drawer_5_p7, row_drawer_5_p8, row_drawer_5_p9, row_drawer_5_p10, row_drawer_5_p11, row_drawer_5_p12, row_drawer_5_p13, row_drawer_5_p14, row_drawer_5_p15, row_drawer_5_p16, row_drawer_5_p17, row_drawer_5_p18, row_drawer_5_p19, row_drawer_5_p20, row_drawer_5_p21, row_drawer_5_p22, row_drawer_5_p23, row_drawer_5_p24, row_drawer_5_p25, row_drawer_5_p26, row_drawer_5_p27, row_drawer_5_p28, row_drawer_5_p29, row_drawer_5_p30, row_drawer_5_p31, row_drawer_5_p32, row_drawer_5_p33, row_drawer_5_p34, row_drawer_5_p35, row_drawer_5_p36, row_drawer_5_p37, row_drawer_5_p38, row_drawer_5_p39, row_drawer_5_p40, row_drawer_5_p41, row_drawer_5_p42, row_drawer_5_p43, row_drawer_5_p44, row_drawer_5_p45, row_drawer_5_p46, row_drawer_5_p47, row_drawer_5_p48, row_drawer_5_p49, row_drawer_5_p50, row_drawer_5_p51, row_drawer_5_p52, row_drawer_5_p53, row_drawer_5_p54, row_drawer_5_p55, row_drawer_5_p56, row_drawer_5_p57, row_drawer_5_p58, row_drawer_5_p59, row_drawer_5_p60, row_drawer_5_p61, row_drawer_5_p62, row_drawer_5_p63, row_drawer_5_p64, row_drawer_5_p65, row_drawer_5_p66
  DotMatrix #(.matrixcols(8)) dotmatrix_5 (
    .col0(row_drawer_5_p3), .col1(row_drawer_5_p4), .col2(row_drawer_5_p5), .col3(row_drawer_5_p6),
    .col4(row_drawer_5_p7), .col5(row_drawer_5_p8), .col6(row_drawer_5_p9), .col7(row_drawer_5_p10));
  DotMatrix #(.matrixcols(8)) dotmatrix_6 (
    .col0(row_drawer_6__00), .col1(row_drawer_6__01), .col2(row_drawer_6__02), .col3(row_drawer_6__03),
    .col4(row_drawer_6__04), .col5(row_drawer_6__05), .col6(row_drawer_6__06), .col7(row_drawer_6__07));
  row_drawer row_drawer_6 (
    ._00(row_drawer_6__00), ._01(row_drawer_6__01), ._02(row_drawer_6__02), ._03(row_drawer_6__03),
    ._04(row_drawer_6__04), ._05(row_drawer_6__05), ._06(row_drawer_6__06), ._07(row_drawer_6__07),
    ._10(row_drawer_6__10), ._11(row_drawer_6__11), ._12(row_drawer_6__12), ._13(row_drawer_6__13),
    ._14(row_drawer_6__14), ._15(row_drawer_6__15), ._16(row_drawer_6__16), ._17(row_drawer_6__17),
    ._20(row_drawer_6__20), ._21(row_drawer_6__21), ._22(row_drawer_6__22), ._23(row_drawer_6__23),
    ._24(row_drawer_6__24), ._25(row_drawer_6__25), ._26(row_drawer_6__26), ._27(row_drawer_6__27),
    ._30(row_drawer_6__30), ._31(row_drawer_6__31), ._32(row_drawer_6__32), ._33(row_drawer_6__33),
    ._34(row_drawer_6__34), ._35(row_drawer_6__35), ._36(row_drawer_6__36), ._37(row_drawer_6__37),
    ._60(row_drawer_6__60), ._61(row_drawer_6__61), ._62(row_drawer_6__62), ._63(row_drawer_6__63),
    ._64(row_drawer_6__64), ._65(row_drawer_6__65), ._66(row_drawer_6__66), ._67(row_drawer_6__67),
    ._70(row_drawer_6__70), ._40(row_drawer_6__40), ._71(row_drawer_6__71), ._41(row_drawer_6__41),
    ._72(row_drawer_6__72), ._42(row_drawer_6__42), ._73(row_drawer_6__73), ._43(row_drawer_6__43),
    ._74(row_drawer_6__74), ._44(row_drawer_6__44), ._75(row_drawer_6__75), ._45(row_drawer_6__45),
    ._76(row_drawer_6__76), ._46(row_drawer_6__46), ._77(row_drawer_6__77), ._47(row_drawer_6__47),
    ._50(row_drawer_6__50), ._51(row_drawer_6__51), ._52(row_drawer_6__52), ._53(row_drawer_6__53),
    ._54(row_drawer_6__54), ._55(row_drawer_6__55), ._56(row_drawer_6__56), ._57(row_drawer_6__57),
    .clk(_5_clk), .data(_5_row_data));  // open: left, right
  DotMatrix #(.matrixcols(8)) dotmatrix_7 (
    .col0(row_drawer_7__00), .col1(row_drawer_7__01), .col2(row_drawer_7__02), .col3(row_drawer_7__03),
    .col4(row_drawer_7__04), .col5(row_drawer_7__05), .col6(row_drawer_7__06), .col7(row_drawer_7__07));
  row_drawer row_drawer_7 (
    ._00(row_drawer_7__00), ._01(row_drawer_7__01), ._02(row_drawer_7__02), ._03(row_drawer_7__03),
    ._04(row_drawer_7__04), ._05(row_drawer_7__05), ._06(row_drawer_7__06), ._07(row_drawer_7__07),
    ._10(row_drawer_7__10), ._11(row_drawer_7__11), ._12(row_drawer_7__12), ._13(row_drawer_7__13),
    ._14(row_drawer_7__14), ._15(row_drawer_7__15), ._16(row_drawer_7__16), ._17(row_drawer_7__17),
    ._20(row_drawer_7__20), ._21(row_drawer_7__21), ._22(row_drawer_7__22), ._23(row_drawer_7__23),
    ._24(row_drawer_7__24), ._25(row_drawer_7__25), ._26(row_drawer_7__26), ._27(row_drawer_7__27),
    ._30(row_drawer_7__30), ._31(row_drawer_7__31), ._32(row_drawer_7__32), ._33(row_drawer_7__33),
    ._34(row_drawer_7__34), ._35(row_drawer_7__35), ._36(row_drawer_7__36), ._37(row_drawer_7__37),
    ._60(row_drawer_7__60), ._61(row_drawer_7__61), ._62(row_drawer_7__62), ._63(row_drawer_7__63),
    ._64(row_drawer_7__64), ._65(row_drawer_7__65), ._66(row_drawer_7__66), ._67(row_drawer_7__67),
    ._70(row_drawer_7__70), ._40(row_drawer_7__40), ._71(row_drawer_7__71), ._41(row_drawer_7__41),
    ._72(row_drawer_7__72), ._42(row_drawer_7__42), ._73(row_drawer_7__73), ._43(row_drawer_7__43),
    ._74(row_drawer_7__74), ._44(row_drawer_7__44), ._75(row_drawer_7__75), ._45(row_drawer_7__45),
    ._76(row_drawer_7__76), ._46(row_drawer_7__46), ._77(row_drawer_7__77), ._47(row_drawer_7__47),
    ._50(row_drawer_7__50), ._51(row_drawer_7__51), ._52(row_drawer_7__52), ._53(row_drawer_7__53),
    ._54(row_drawer_7__54), ._55(row_drawer_7__55), ._56(row_drawer_7__56), ._57(row_drawer_7__57),
    .clk(_6_clk), .data(_6_row_data));  // open: left, right
  row_drawer row_drawer_8 (
    ._00(row_drawer_8__00), ._01(row_drawer_8__01), ._02(row_drawer_8__02), ._03(row_drawer_8__03),
    ._04(row_drawer_8__04), ._05(row_drawer_8__05), ._06(row_drawer_8__06), ._07(row_drawer_8__07),
    ._10(row_drawer_8__10), ._11(row_drawer_8__11), ._12(row_drawer_8__12), ._13(row_drawer_8__13),
    ._14(row_drawer_8__14), ._15(row_drawer_8__15), ._16(row_drawer_8__16), ._17(row_drawer_8__17),
    ._20(row_drawer_8__20), ._21(row_drawer_8__21), ._22(row_drawer_8__22), ._23(row_drawer_8__23),
    ._24(row_drawer_8__24), ._25(row_drawer_8__25), ._26(row_drawer_8__26), ._27(row_drawer_8__27),
    ._30(row_drawer_8__30), ._31(row_drawer_8__31), ._32(row_drawer_8__32), ._33(row_drawer_8__33),
    ._34(row_drawer_8__34), ._35(row_drawer_8__35), ._36(row_drawer_8__36), ._37(row_drawer_8__37),
    ._60(row_drawer_8__60), ._61(row_drawer_8__61), ._62(row_drawer_8__62), ._63(row_drawer_8__63),
    ._64(row_drawer_8__64), ._65(row_drawer_8__65), ._66(row_drawer_8__66), ._67(row_drawer_8__67),
    ._70(row_drawer_8__70), ._40(row_drawer_8__40), ._71(row_drawer_8__71), ._41(row_drawer_8__41),
    ._72(row_drawer_8__72), ._42(row_drawer_8__42), ._73(row_drawer_8__73), ._43(row_drawer_8__43),
    ._74(row_drawer_8__74), ._44(row_drawer_8__44), ._75(row_drawer_8__75), ._45(row_drawer_8__45),
    ._76(row_drawer_8__76), ._46(row_drawer_8__46), ._77(row_drawer_8__77), ._47(row_drawer_8__47),
    ._50(row_drawer_8__50), ._51(row_drawer_8__51), ._52(row_drawer_8__52), ._53(row_drawer_8__53),
    ._54(row_drawer_8__54), ._55(row_drawer_8__55), ._56(row_drawer_8__56), ._57(row_drawer_8__57),
    .clk(_7_clk), .data(_7_left));  // open: left, right
  DotMatrix #(.matrixcols(8)) dotmatrix_8 (
    .col0(row_drawer_8__00), .col1(row_drawer_8__01), .col2(row_drawer_8__02), .col3(row_drawer_8__03),
    .col4(row_drawer_8__04), .col5(row_drawer_8__05), .col6(row_drawer_8__06), .col7(row_drawer_8__07));
  DotMatrix #(.matrixcols(8)) dotmatrix_9 (
    .col0(row_drawer_1__10), .col1(row_drawer_1__11), .col2(row_drawer_1__12), .col3(row_drawer_1__13),
    .col4(row_drawer_1__14), .col5(row_drawer_1__15), .col6(row_drawer_1__16), .col7(row_drawer_1__17));
  DotMatrix #(.matrixcols(8)) dotmatrix_10 (
    .col0(row_drawer_2__10), .col1(row_drawer_2__11), .col2(row_drawer_2__12), .col3(row_drawer_2__13),
    .col4(row_drawer_2__14), .col5(row_drawer_2__15), .col6(row_drawer_2__16), .col7(row_drawer_2__17));
  DotMatrix #(.matrixcols(8)) dotmatrix_11 (
    .col0(row_drawer_3__10), .col1(row_drawer_3__11), .col2(row_drawer_3__12), .col3(row_drawer_3__13),
    .col4(row_drawer_3__14), .col5(row_drawer_3__15), .col6(row_drawer_3__16), .col7(row_drawer_3__17));
  DotMatrix #(.matrixcols(8)) dotmatrix_12 (
    .col0(row_drawer_4__10), .col1(row_drawer_4__11), .col2(row_drawer_4__12), .col3(row_drawer_4__13),
    .col4(row_drawer_4__14), .col5(row_drawer_4__15), .col6(row_drawer_4__16), .col7(row_drawer_4__17));
  DotMatrix #(.matrixcols(8)) dotmatrix_13 (
    .col0(row_drawer_5_p11), .col1(row_drawer_5_p12), .col2(row_drawer_5_p13), .col3(row_drawer_5_p14),
    .col4(row_drawer_5_p15), .col5(row_drawer_5_p16), .col6(row_drawer_5_p17), .col7(row_drawer_5_p18));
  DotMatrix #(.matrixcols(8)) dotmatrix_14 (
    .col0(row_drawer_6__10), .col1(row_drawer_6__11), .col2(row_drawer_6__12), .col3(row_drawer_6__13),
    .col4(row_drawer_6__14), .col5(row_drawer_6__15), .col6(row_drawer_6__16), .col7(row_drawer_6__17));
  DotMatrix #(.matrixcols(8)) dotmatrix_15 (
    .col0(row_drawer_7__10), .col1(row_drawer_7__11), .col2(row_drawer_7__12), .col3(row_drawer_7__13),
    .col4(row_drawer_7__14), .col5(row_drawer_7__15), .col6(row_drawer_7__16), .col7(row_drawer_7__17));
  DotMatrix #(.matrixcols(8)) dotmatrix_16 (
    .col0(row_drawer_8__10), .col1(row_drawer_8__11), .col2(row_drawer_8__12), .col3(row_drawer_8__13),
    .col4(row_drawer_8__14), .col5(row_drawer_8__15), .col6(row_drawer_8__16), .col7(row_drawer_8__17));
  DotMatrix #(.matrixcols(8)) dotmatrix_17 (
    .col0(row_drawer_1__20), .col1(row_drawer_1__21), .col2(row_drawer_1__22), .col3(row_drawer_1__23),
    .col4(row_drawer_1__24), .col5(row_drawer_1__25), .col6(row_drawer_1__26), .col7(row_drawer_1__27));
  DotMatrix #(.matrixcols(8)) dotmatrix_18 (
    .col0(row_drawer_2__20), .col1(row_drawer_2__21), .col2(row_drawer_2__22), .col3(row_drawer_2__23),
    .col4(row_drawer_2__24), .col5(row_drawer_2__25), .col6(row_drawer_2__26), .col7(row_drawer_2__27));
  DotMatrix #(.matrixcols(8)) dotmatrix_19 (
    .col0(row_drawer_3__20), .col1(row_drawer_3__21), .col2(row_drawer_3__22), .col3(row_drawer_3__23),
    .col4(row_drawer_3__24), .col5(row_drawer_3__25), .col6(row_drawer_3__26), .col7(row_drawer_3__27));
  DotMatrix #(.matrixcols(8)) dotmatrix_20 (
    .col0(row_drawer_4__20), .col1(row_drawer_4__21), .col2(row_drawer_4__22), .col3(row_drawer_4__23),
    .col4(row_drawer_4__24), .col5(row_drawer_4__25), .col6(row_drawer_4__26), .col7(row_drawer_4__27));
  DotMatrix #(.matrixcols(8)) dotmatrix_21 (
    .col0(row_drawer_5_p19), .col1(row_drawer_5_p20), .col2(row_drawer_5_p21), .col3(row_drawer_5_p22),
    .col4(row_drawer_5_p23), .col5(row_drawer_5_p24), .col6(row_drawer_5_p25), .col7(row_drawer_5_p26));
  DotMatrix #(.matrixcols(8)) dotmatrix_22 (
    .col0(row_drawer_6__20), .col1(row_drawer_6__21), .col2(row_drawer_6__22), .col3(row_drawer_6__23),
    .col4(row_drawer_6__24), .col5(row_drawer_6__25), .col6(row_drawer_6__26), .col7(row_drawer_6__27));
  DotMatrix #(.matrixcols(8)) dotmatrix_23 (
    .col0(row_drawer_7__20), .col1(row_drawer_7__21), .col2(row_drawer_7__22), .col3(row_drawer_7__23),
    .col4(row_drawer_7__24), .col5(row_drawer_7__25), .col6(row_drawer_7__26), .col7(row_drawer_7__27));
  DotMatrix #(.matrixcols(8)) dotmatrix_24 (
    .col0(row_drawer_8__20), .col1(row_drawer_8__21), .col2(row_drawer_8__22), .col3(row_drawer_8__23),
    .col4(row_drawer_8__24), .col5(row_drawer_8__25), .col6(row_drawer_8__26), .col7(row_drawer_8__27));
  DotMatrix #(.matrixcols(8)) dotmatrix_25 (
    .col0(row_drawer_1__30), .col1(row_drawer_1__31), .col2(row_drawer_1__32), .col3(row_drawer_1__33),
    .col4(row_drawer_1__34), .col5(row_drawer_1__35), .col6(row_drawer_1__36), .col7(row_drawer_1__37));
  DotMatrix #(.matrixcols(8)) dotmatrix_26 (
    .col0(row_drawer_2__30), .col1(row_drawer_2__31), .col2(row_drawer_2__32), .col3(row_drawer_2__33),
    .col4(row_drawer_2__34), .col5(row_drawer_2__35), .col6(row_drawer_2__36), .col7(row_drawer_2__37));
  DotMatrix #(.matrixcols(8)) dotmatrix_27 (
    .col0(row_drawer_3__30), .col1(row_drawer_3__31), .col2(row_drawer_3__32), .col3(row_drawer_3__33),
    .col4(row_drawer_3__34), .col5(row_drawer_3__35), .col6(row_drawer_3__36), .col7(row_drawer_3__37));
  DotMatrix #(.matrixcols(8)) dotmatrix_28 (
    .col0(row_drawer_4__30), .col1(row_drawer_4__31), .col2(row_drawer_4__32), .col3(row_drawer_4__33),
    .col4(row_drawer_4__34), .col5(row_drawer_4__35), .col6(row_drawer_4__36), .col7(row_drawer_4__37));
  DotMatrix #(.matrixcols(8)) dotmatrix_29 (
    .col0(row_drawer_5_p27), .col1(row_drawer_5_p28), .col2(row_drawer_5_p29), .col3(row_drawer_5_p30),
    .col4(row_drawer_5_p31), .col5(row_drawer_5_p32), .col6(row_drawer_5_p33), .col7(row_drawer_5_p34));
  DotMatrix #(.matrixcols(8)) dotmatrix_30 (
    .col0(row_drawer_6__30), .col1(row_drawer_6__31), .col2(row_drawer_6__32), .col3(row_drawer_6__33),
    .col4(row_drawer_6__34), .col5(row_drawer_6__35), .col6(row_drawer_6__36), .col7(row_drawer_6__37));
  DotMatrix #(.matrixcols(8)) dotmatrix_31 (
    .col0(row_drawer_7__30), .col1(row_drawer_7__31), .col2(row_drawer_7__32), .col3(row_drawer_7__33),
    .col4(row_drawer_7__34), .col5(row_drawer_7__35), .col6(row_drawer_7__36), .col7(row_drawer_7__37));
  DotMatrix #(.matrixcols(8)) dotmatrix_32 (
    .col0(row_drawer_8__30), .col1(row_drawer_8__31), .col2(row_drawer_8__32), .col3(row_drawer_8__33),
    .col4(row_drawer_8__34), .col5(row_drawer_8__35), .col6(row_drawer_8__36), .col7(row_drawer_8__37));
  DotMatrix #(.matrixcols(8)) dotmatrix_33 (
    .col0(row_drawer_1__40), .col1(row_drawer_1__41), .col2(row_drawer_1__42), .col3(row_drawer_1__43),
    .col4(row_drawer_1__44), .col5(row_drawer_1__45), .col6(row_drawer_1__46), .col7(row_drawer_1__47));
  DotMatrix #(.matrixcols(8)) dotmatrix_34 (
    .col0(row_drawer_2__40), .col1(row_drawer_2__41), .col2(row_drawer_2__42), .col3(row_drawer_2__43),
    .col4(row_drawer_2__44), .col5(row_drawer_2__45), .col6(row_drawer_2__46), .col7(row_drawer_2__47));
  DotMatrix #(.matrixcols(8)) dotmatrix_35 (
    .col0(row_drawer_3__40), .col1(row_drawer_3__41), .col2(row_drawer_3__42), .col3(row_drawer_3__43),
    .col4(row_drawer_3__44), .col5(row_drawer_3__45), .col6(row_drawer_3__46), .col7(row_drawer_3__47));
  DotMatrix #(.matrixcols(8)) dotmatrix_36 (
    .col0(row_drawer_4__40), .col1(row_drawer_4__41), .col2(row_drawer_4__42), .col3(row_drawer_4__43),
    .col4(row_drawer_4__44), .col5(row_drawer_4__45), .col6(row_drawer_4__46), .col7(row_drawer_4__47));
  DotMatrix #(.matrixcols(8)) dotmatrix_37 (
    .col0(row_drawer_5_p35), .col1(row_drawer_5_p36), .col2(row_drawer_5_p37), .col3(row_drawer_5_p38),
    .col4(row_drawer_5_p39), .col5(row_drawer_5_p40), .col6(row_drawer_5_p41), .col7(row_drawer_5_p42));
  DotMatrix #(.matrixcols(8)) dotmatrix_38 (
    .col0(row_drawer_6__40), .col1(row_drawer_6__41), .col2(row_drawer_6__42), .col3(row_drawer_6__43),
    .col4(row_drawer_6__44), .col5(row_drawer_6__45), .col6(row_drawer_6__46), .col7(row_drawer_6__47));
  DotMatrix #(.matrixcols(8)) dotmatrix_39 (
    .col0(row_drawer_7__40), .col1(row_drawer_7__41), .col2(row_drawer_7__42), .col3(row_drawer_7__43),
    .col4(row_drawer_7__44), .col5(row_drawer_7__45), .col6(row_drawer_7__46), .col7(row_drawer_7__47));
  DotMatrix #(.matrixcols(8)) dotmatrix_40 (
    .col0(row_drawer_8__40), .col1(row_drawer_8__41), .col2(row_drawer_8__42), .col3(row_drawer_8__43),
    .col4(row_drawer_8__44), .col5(row_drawer_8__45), .col6(row_drawer_8__46), .col7(row_drawer_8__47));
  DotMatrix #(.matrixcols(8)) dotmatrix_41 (
    .col0(row_drawer_1__50), .col1(row_drawer_1__51), .col2(row_drawer_1__52), .col3(row_drawer_1__53),
    .col4(row_drawer_1__54), .col5(row_drawer_1__55), .col6(row_drawer_1__56), .col7(row_drawer_1__57));
  DotMatrix #(.matrixcols(8)) dotmatrix_42 (
    .col0(row_drawer_2__50), .col1(row_drawer_2__51), .col2(row_drawer_2__52), .col3(row_drawer_2__53),
    .col4(row_drawer_2__54), .col5(row_drawer_2__55), .col6(row_drawer_2__56), .col7(row_drawer_2__57));
  DotMatrix #(.matrixcols(8)) dotmatrix_43 (
    .col0(row_drawer_3__50), .col1(row_drawer_3__51), .col2(row_drawer_3__52), .col3(row_drawer_3__53),
    .col4(row_drawer_3__54), .col5(row_drawer_3__55), .col6(row_drawer_3__56), .col7(row_drawer_3__57));
  DotMatrix #(.matrixcols(8)) dotmatrix_44 (
    .col0(row_drawer_4__50), .col1(row_drawer_4__51), .col2(row_drawer_4__52), .col3(row_drawer_4__53),
    .col4(row_drawer_4__54), .col5(row_drawer_4__55), .col6(row_drawer_4__56), .col7(row_drawer_4__57));
  DotMatrix #(.matrixcols(8)) dotmatrix_45 (
    .col0(row_drawer_5_p43), .col1(row_drawer_5_p44), .col2(row_drawer_5_p45), .col3(row_drawer_5_p46),
    .col4(row_drawer_5_p47), .col5(row_drawer_5_p48), .col6(row_drawer_5_p49), .col7(row_drawer_5_p50));
  DotMatrix #(.matrixcols(8)) dotmatrix_46 (
    .col0(row_drawer_6__50), .col1(row_drawer_6__51), .col2(row_drawer_6__52), .col3(row_drawer_6__53),
    .col4(row_drawer_6__54), .col5(row_drawer_6__55), .col6(row_drawer_6__56), .col7(row_drawer_6__57));
  DotMatrix #(.matrixcols(8)) dotmatrix_47 (
    .col0(row_drawer_7__50), .col1(row_drawer_7__51), .col2(row_drawer_7__52), .col3(row_drawer_7__53),
    .col4(row_drawer_7__54), .col5(row_drawer_7__55), .col6(row_drawer_7__56), .col7(row_drawer_7__57));
  DotMatrix #(.matrixcols(8)) dotmatrix_48 (
    .col0(row_drawer_8__50), .col1(row_drawer_8__51), .col2(row_drawer_8__52), .col3(row_drawer_8__53),
    .col4(row_drawer_8__54), .col5(row_drawer_8__55), .col6(row_drawer_8__56), .col7(row_drawer_8__57));
  DotMatrix #(.matrixcols(8)) dotmatrix_49 (
    .col0(row_drawer_1__60), .col1(row_drawer_1__61), .col2(row_drawer_1__62), .col3(row_drawer_1__63),
    .col4(row_drawer_1__64), .col5(row_drawer_1__65), .col6(row_drawer_1__66), .col7(row_drawer_1__67));
  DotMatrix #(.matrixcols(8)) dotmatrix_50 (
    .col0(row_drawer_2__60), .col1(row_drawer_2__61), .col2(row_drawer_2__62), .col3(row_drawer_2__63),
    .col4(row_drawer_2__64), .col5(row_drawer_2__65), .col6(row_drawer_2__66), .col7(row_drawer_2__67));
  DotMatrix #(.matrixcols(8)) dotmatrix_51 (
    .col0(row_drawer_3__60), .col1(row_drawer_3__61), .col2(row_drawer_3__62), .col3(row_drawer_3__63),
    .col4(row_drawer_3__64), .col5(row_drawer_3__65), .col6(row_drawer_3__66), .col7(row_drawer_3__67));
  DotMatrix #(.matrixcols(8)) dotmatrix_52 (
    .col0(row_drawer_4__60), .col1(row_drawer_4__61), .col2(row_drawer_4__62), .col3(row_drawer_4__63),
    .col4(row_drawer_4__64), .col5(row_drawer_4__65), .col6(row_drawer_4__66), .col7(row_drawer_4__67));
  DotMatrix #(.matrixcols(8)) dotmatrix_53 (
    .col0(row_drawer_5_p51), .col1(row_drawer_5_p52), .col2(row_drawer_5_p53), .col3(row_drawer_5_p54),
    .col4(row_drawer_5_p55), .col5(row_drawer_5_p56), .col6(row_drawer_5_p57), .col7(row_drawer_5_p58));
  DotMatrix #(.matrixcols(8)) dotmatrix_54 (
    .col0(row_drawer_6__60), .col1(row_drawer_6__61), .col2(row_drawer_6__62), .col3(row_drawer_6__63),
    .col4(row_drawer_6__64), .col5(row_drawer_6__65), .col6(row_drawer_6__66), .col7(row_drawer_6__67));
  DotMatrix #(.matrixcols(8)) dotmatrix_55 (
    .col0(row_drawer_7__60), .col1(row_drawer_7__61), .col2(row_drawer_7__62), .col3(row_drawer_7__63),
    .col4(row_drawer_7__64), .col5(row_drawer_7__65), .col6(row_drawer_7__66), .col7(row_drawer_7__67));
  DotMatrix #(.matrixcols(8)) dotmatrix_56 (
    .col0(row_drawer_8__60), .col1(row_drawer_8__61), .col2(row_drawer_8__62), .col3(row_drawer_8__63),
    .col4(row_drawer_8__64), .col5(row_drawer_8__65), .col6(row_drawer_8__66), .col7(row_drawer_8__67));
  DotMatrix #(.matrixcols(8)) dotmatrix_57 (
    .col0(row_drawer_1__70), .col1(row_drawer_1__71), .col2(row_drawer_1__72), .col3(row_drawer_1__73),
    .col4(row_drawer_1__74), .col5(row_drawer_1__75), .col6(row_drawer_1__76), .col7(row_drawer_1__77));
  DotMatrix #(.matrixcols(8)) dotmatrix_58 (
    .col0(row_drawer_2__70), .col1(row_drawer_2__71), .col2(row_drawer_2__72), .col3(row_drawer_2__73),
    .col4(row_drawer_2__74), .col5(row_drawer_2__75), .col6(row_drawer_2__76), .col7(row_drawer_2__77));
  DotMatrix #(.matrixcols(8)) dotmatrix_59 (
    .col0(row_drawer_3__70), .col1(row_drawer_3__71), .col2(row_drawer_3__72), .col3(row_drawer_3__73),
    .col4(row_drawer_3__74), .col5(row_drawer_3__75), .col6(row_drawer_3__76), .col7(row_drawer_3__77));
  DotMatrix #(.matrixcols(8)) dotmatrix_60 (
    .col0(row_drawer_4__70), .col1(row_drawer_4__71), .col2(row_drawer_4__72), .col3(row_drawer_4__73),
    .col4(row_drawer_4__74), .col5(row_drawer_4__75), .col6(row_drawer_4__76), .col7(row_drawer_4__77));
  DotMatrix #(.matrixcols(8)) dotmatrix_61 (
    .col0(row_drawer_5_p59), .col1(row_drawer_5_p60), .col2(row_drawer_5_p61), .col3(row_drawer_5_p62),
    .col4(row_drawer_5_p63), .col5(row_drawer_5_p64), .col6(row_drawer_5_p65), .col7(row_drawer_5_p66));
  DotMatrix #(.matrixcols(8)) dotmatrix_62 (
    .col0(row_drawer_6__70), .col1(row_drawer_6__71), .col2(row_drawer_6__72), .col3(row_drawer_6__73),
    .col4(row_drawer_6__74), .col5(row_drawer_6__75), .col6(row_drawer_6__76), .col7(row_drawer_6__77));
  DotMatrix #(.matrixcols(8)) dotmatrix_63 (
    .col0(row_drawer_7__70), .col1(row_drawer_7__71), .col2(row_drawer_7__72), .col3(row_drawer_7__73),
    .col4(row_drawer_7__74), .col5(row_drawer_7__75), .col6(row_drawer_7__76), .col7(row_drawer_7__77));
  DotMatrix #(.matrixcols(8)) dotmatrix_64 (
    .col0(row_drawer_8__70), .col1(row_drawer_8__71), .col2(row_drawer_8__72), .col3(row_drawer_8__73),
    .col4(row_drawer_8__74), .col5(row_drawer_8__75), .col6(row_drawer_8__76), .col7(row_drawer_8__77));
  Clock clock_1 (.out(clk));
  controller controller_1 (
    .reset(reset), .up(up), .left(left), .down(down), .right(right), .open(open), .flag(flag),
    .IRQ(controller_1_irq), .vec(controller_1_vec));
  processor_hadnler processor_hadnler_1 (
    .IRQ(controller_1_irq), .vec(controller_1_vec), .reset(reset), .clk(clk));  // open: row_out, row_num, st_row_out
  video_handler video_handler_1 ();  // open: data, row_num, clk, left_clk, right_clk, clk_0, clk_1, clk_2, clk_3, clk_4, clk_5, clk_6, clk_7
endmodule

module processor_hadnler (
  input  IRQ,
  input  [2:0] vec,
  input  clk,
  input  reset,
  output [31:0] row_out,
  output [3:0] row_num,
  output st_row_out
);

  wire and_2_out, and_3_out, cdm_8_mark5_1_data_inst, cdm_8_mark5_1_mem_cycle, cell_0_upd, cell_1_upd,
       cell_2_upd, clk_t, decoder_1_out0, decoder_1_out1, decoder_1_out2, decoder_1_out3, delayer_1_second,
       IAck, map_loaded, map_register_full, map_sel, multiplexer_2_out, not_1_out, not_2_out, not_3_out,
       or_1_out, or_2_out, or_3_out, or_4_out, or_5_out, program_sel, wr;
  wire [6:0] cell_drawer_1_row_0, cell_drawer_1_row_1, cell_drawer_1_row_2, cell_drawer_1_row_3,
       cell_drawer_1_row_4, cell_drawer_1_row_5, cell_drawer_1_row_6, cell_drawer_1_row_7,
       cell_drawer_2_row_0, cell_drawer_2_row_1, cell_drawer_2_row_2, cell_drawer_2_row_3,
       cell_drawer_2_row_4, cell_drawer_2_row_5, cell_drawer_2_row_6, cell_drawer_2_row_7,
       cell_drawer_3_row_0, cell_drawer_3_row_1, cell_drawer_3_row_2, cell_drawer_3_row_3,
       cell_drawer_3_row_4, cell_drawer_3_row_5, cell_drawer_3_row_6, cell_drawer_3_row_7,
       cell_drawer_4_row_0, cell_drawer_4_row_1, cell_drawer_4_row_2, cell_drawer_4_row_3,
       cell_drawer_4_row_4, cell_drawer_4_row_5, cell_drawer_4_row_6, cell_drawer_4_row_7;
  wire [7:0] addr, cdm_8_mark5_1_data_out, cdm_8_mark5_1_pc, cdm_8_mark5_1_ps, cdm_8_mark5_1_r0,
       cdm_8_mark5_1_r1, cdm_8_mark5_1_r2, cdm_8_mark5_1_r3, cdm_8_mark5_1_sp, data, divider_1_rem,
       map_loader_1_data, map_offsest, multiplexer_1_out, ram_1_data, undriven;
  wire [7:4] map_loader_addr;

  map_loader map_loader_1 (
    .clk(clk_t), .reset(reset), .loaded(map_loaded), .data(map_loader_1_data), .addr(map_offsest));
  delayer delayer_1 (.bus_0(reset), .second(delayer_1_second));  // open: first
  not not_1 (not_1_out, map_loaded);
  Divider divider_1 (.a(map_offsest), .b(8'h4), .rem(divider_1_rem));  // open: out, upper
  // Probe on divider_1_rem[1:0]
  and and_1 (map_register_full, divider_1_rem[0], divider_1_rem[1]);
  and and_2 (and_2_out, program_sel, map_loaded);
  Decoder #(.select(2)) decoder_1 (
    .out0(decoder_1_out0), .out1(decoder_1_out1), .out2(decoder_1_out2), .out3(decoder_1_out3),
    .sel(divider_1_rem[1:0]));  // open: en
  or or_1 (or_1_out, cell_0_upd, delayer_1_second);
  or or_2 (or_2_out, cell_1_upd, delayer_1_second);
  or or_3 (or_3_out, cell_2_upd, delayer_1_second);
  or or_4 (or_4_out, st_row_out, delayer_1_second);
  ROM rom_1 (.addr(addr), .data(data), .sel(and_2_out));
  Register register_1 (.D(map_loader_1_data), .en(not_1_out), .Q(row_out[15:8]), .clk(decoder_1_out1), .clr(reset));
  Register register_2 (.D(map_loader_1_data), .en(not_1_out), .Q(row_out[7:0]), .clk(decoder_1_out0), .clr(reset));
  delayer delayer_2 (.bus_0(decoder_1_out0), .second(cell_0_upd));  // open: first
  delayer delayer_3 (.bus_0(decoder_1_out1), .second(cell_1_upd));  // open: first
  Register register_3 (.D(map_loader_1_data), .en(not_1_out), .Q(row_out[23:16]), .clk(decoder_1_out2), .clr(reset));
  delayer delayer_4 (.bus_0(decoder_1_out2), .second(cell_2_upd));  // open: first
  cell_drawer cell_drawer_1 (
    .cell_data(row_out[7:0]), .clk(or_1_out), .row_0(cell_drawer_1_row_0), .row_1(cell_drawer_1_row_1),
    .row_2(cell_drawer_1_row_2), .row_3(cell_drawer_1_row_3), .row_4(cell_drawer_1_row_4),
    .row_5(cell_drawer_1_row_5), .row_6(cell_drawer_1_row_6), .row_7(cell_drawer_1_row_7));
  DotMatrix #(.matrixcols(8)) dotmatrix_1 (
    .col0(cell_drawer_1_row_0), .col1(cell_drawer_1_row_1), .col2(cell_drawer_1_row_2),
    .col3(cell_drawer_1_row_3), .col4(cell_drawer_1_row_4), .col5(cell_drawer_1_row_5),
    .col6(cell_drawer_1_row_6), .col7(cell_drawer_1_row_7));
  // Probe on row_out[7:0]
  // Probe on row_out[15:8]
  // Probe on row_out[23:16]
  // Probe on cdm_8_mark5_1_r2
  // Probe on cdm_8_mark5_1_r1
  // Probe on cdm_8_mark5_1_r0
  Register register_4 (.D(map_loader_1_data), .en(not_1_out), .Q(row_out[31:24]), .clk(decoder_1_out3), .clr(reset));
  delayer delayer_5 (.bus_0(decoder_1_out3), .second(st_row_out));  // open: first
  cell_drawer cell_drawer_2 (
    .cell_data(row_out[15:8]), .clk(or_2_out), .row_0(cell_drawer_2_row_0), .row_1(cell_drawer_2_row_1),
    .row_2(cell_drawer_2_row_2), .row_3(cell_drawer_2_row_3), .row_4(cell_drawer_2_row_4),
    .row_5(cell_drawer_2_row_5), .row_6(cell_drawer_2_row_6), .row_7(cell_drawer_2_row_7));
  DotMatrix #(.matrixcols(8)) dotmatrix_2 (
    .col0(cell_drawer_2_row_0), .col1(cell_drawer_2_row_1), .col2(cell_drawer_2_row_2),
    .col3(cell_drawer_2_row_3), .col4(cell_drawer_2_row_4), .col5(cell_drawer_2_row_5),
    .col6(cell_drawer_2_row_6), .col7(cell_drawer_2_row_7));
  // Probe on row_out[31:24]
  // Probe on cdm_8_mark5_1_r3
  // Probe on cdm_8_mark5_1_pc
  // Probe on cdm_8_mark5_1_sp
  // Probe on cdm_8_mark5_1_ps
  cell_drawer cell_drawer_3 (
    .cell_data(row_out[23:16]), .clk(or_3_out), .row_0(cell_drawer_3_row_0), .row_1(cell_drawer_3_row_1),
    .row_2(cell_drawer_3_row_2), .row_3(cell_drawer_3_row_3), .row_4(cell_drawer_3_row_4),
    .row_5(cell_drawer_3_row_5), .row_6(cell_drawer_3_row_6), .row_7(cell_drawer_3_row_7));
  DotMatrix #(.matrixcols(8)) dotmatrix_3 (
    .col0(cell_drawer_3_row_0), .col1(cell_drawer_3_row_1), .col2(cell_drawer_3_row_2),
    .col3(cell_drawer_3_row_3), .col4(cell_drawer_3_row_4), .col5(cell_drawer_3_row_5),
    .col6(cell_drawer_3_row_6), .col7(cell_drawer_3_row_7));
  Decoder decoder_2 (.out0(program_sel), .out1(map_sel), .sel(cdm_8_mark5_1_data_inst), .en(cdm_8_mark5_1_mem_cycle));
  CdM_8_mark5 cdm_8_mark5_1 (
    .clock(clk), .addr(addr), .mem_read(wr), .mem_cycle(cdm_8_mark5_1_mem_cycle),
    .data_inst(cdm_8_mark5_1_data_inst), .data_out(cdm_8_mark5_1_data_out), .data_in(undriven),
    .r0(cdm_8_mark5_1_r0), .r1(cdm_8_mark5_1_r1), .r2(cdm_8_mark5_1_r2), .r3(cdm_8_mark5_1_r3),
    .PC(cdm_8_mark5_1_pc), .SP(cdm_8_mark5_1_sp), .PS(cdm_8_mark5_1_ps), .IAck(IAck), .IRQ(IRQ), .vec(vec));
  assign cdm_8_mark5_1_data_out = wr ? data : 8'bz;  // Controlled_Buffer controlled_buffer_1
  assign data = not_2_out ? undriven : 8'bz;  // Controlled_Buffer controlled_buffer_2
  not not_2 (not_2_out, wr);
  DotMatrix #(.matrixcols(8)) dotmatrix_4 (
    .col0(cell_drawer_4_row_0), .col1(cell_drawer_4_row_1), .col2(cell_drawer_4_row_2),
    .col3(cell_drawer_4_row_3), .col4(cell_drawer_4_row_4), .col5(cell_drawer_4_row_5),
    .col6(cell_drawer_4_row_6), .col7(cell_drawer_4_row_7));
  cell_drawer cell_drawer_4 (
    .cell_data(row_out[31:24]), .clk(or_4_out), .row_0(cell_drawer_4_row_0), .row_1(cell_drawer_4_row_1),
    .row_2(cell_drawer_4_row_2), .row_3(cell_drawer_4_row_3), .row_4(cell_drawer_4_row_4),
    .row_5(cell_drawer_4_row_5), .row_6(cell_drawer_4_row_6), .row_7(cell_drawer_4_row_7));
  Counter counter_1 (.Q({map_loader_addr, row_num}), .clk(st_row_out), .clr(reset));  // open: load, D, count, carry
  Multiplexer #(.width(8)) multiplexer_1 (
    .in0({map_loader_addr, row_num}), .in1(addr), .out(multiplexer_1_out), .sel(map_loaded));  // open: en
  // Probe on multiplexer_1_out
  or or_5 (or_5_out, ~map_loaded, map_sel);  // OR_Gate
  Pull_Resistor pull_resistor_1 (.node(map_sel));
  not not_3 (not_3_out, clk);
  RAM ram_1 (
    .addr(multiplexer_1_out), .data(ram_1_data), .sel(or_5_out), .clk(multiplexer_2_out), .ld(and_3_out),
    .clr(reset));
  Multiplexer multiplexer_2 (.in0(st_row_out), .in1(not_3_out), .out(multiplexer_2_out), .sel(map_loaded));  // open: en
  Multiplexer #(.width(8)) multiplexer_3 (
    .in0({1'b0, row_out[27], 1'b0, row_out[19], 1'b0, row_out[11], 1'b0, row_out[3]}), .in1(data),
    .out(ram_1_data), .sel(map_loaded));  // open: en
  and and_3 (and_3_out, wr, map_loaded);

  // Other names for the same wires on the sheet: cell_3_upd = st_row_out; map_loader_addr[3:0] = row_num;
  //   cell_0[7:0] = row_out[7:0]; mapped_cell (some bits) = {row_out[27], row_out[19], row_out[11], row_out[3]};
  //   cell_1[7:0] = row_out[15:8]; cell_2[7:0] = row_out[23:16]; cell_3[7:0] = row_out[31:24]

  // Notes on the sheet:
  //   program
  //   map
endmodule

module map_selector (
  input  [7:0] addr,
  input  sel,
  input  clk,
  output [7:0] cell_info
);

  wire [7:0] addr_t, data_0, data_1, data_2, data_3, data_4, data_5, data_6, data_7, multiplier_1_out,
       offset, seed;

  ROM rom_1 (.addr(addr_t), .data(data_0), .sel(sel));
  ROM rom_2 (.addr(addr_t), .data(data_1), .sel(sel));
  ROM rom_3 (.addr(addr_t), .data(data_2), .sel(sel));
  ROM rom_4 (.addr(addr_t), .data(data_3), .sel(sel));
  ROM rom_5 (.addr(addr_t), .data(data_4), .sel(sel));
  ROM rom_6 (.addr(addr_t), .data(data_5), .sel(sel));
  ROM rom_7 (.addr(addr_t), .data(data_6), .sel(sel));
  ROM rom_8 (.addr(addr_t), .data(data_7), .sel(sel));
  Adder adder_1 (.a(addr), .b(multiplier_1_out), .out(addr_t));  // open: cin, cout
  Multiplier multiplier_1 (.a(offset), .b(8'h40), .out(multiplier_1_out));  // open: cin, cout
  Multiplexer #(.select(3), .width(8)) multiplexer_1 (
    .in0(data_0), .in1(data_1), .in2(data_2), .in3(data_3), .in4(data_4), .in5(data_5), .in6(data_6),
    .in7(data_7), .out(cell_info), .sel(3'b000));  // open: en
  Multiplexer #(.select(2), .width(8)) multiplexer_2 (
    .in0({8{1'b0}}), .in1(8'h1), .in2(8'h2), .in3(8'h3), .out(offset), .sel(2'b00));  // open: en
  Random random_1 (.clk(clk), .out(seed));  // open: next, clr

  // Other names for the same wires on the sheet: row_addr[7:0] = addr

  // Notes on the sheet:
  //   contents of rom_1 (hex, n*v repeats v):
  //   40 41 42 43 44 45 46 47 60 61 62 63 64 65 66 67 48 68 10 30 20 0 20 0 20 0 20 0 20 0 20 0 20 0 20 0
  //   20 0 20 0 20 0 20 0 20 0 20 0 20 0 20 0 20 0 20 0 20 0 20 0 20 0 20 0 40 41 42 43 44 45 46 47 60 61
  //   62 63 64 65 66 67 48 68 10 30 20 0 20 0 20 0 20 0 20 0 20 0 20 0 20 0 20 0 20 0 20 0 20 0 20 0 20 0
  //   20 0 20 0 20 0 20 0 20 0 20 0 20 0 20 0 40 41 42 43 44 45 46 47 60 61 62 63 64 65 66 67 48 68 10 30
  //   20 0 20 0 20 0 20 0 20 0 20 0 20 0 20 0 20 0 20 0 20 0 20 0 20 0 20 0 20 0 20 0 20 0 20 0 20 0 20 0
  //   20 0 20 0 40 41 42 43 44 45 46 47 60 61 62 63 64 65 66 67 48 68 10 30 20 0 20 0 20 0 20 0 20 0 20 0
  //   20 0 20 0 20 0 20 0 20 0 20 0 20 0 20 0 20 0 20 0 20 0 20 0 20 0 20 0 20 0 20
endmodule

module controller (
  input  reset,
  input  up,
  input  left,
  input  down,
  input  right,
  input  open,
  input  flag,
  output IRQ,
  output [2:0] vec
);

  or or_1 (IRQ, reset, up, left, down, right, open, flag);
  Multiplexer #(.select(3), .width(3)) multiplexer_1 (
    .in0(3'b000), .in1(3'b000), .in2(3'b000), .in3(3'b000), .in4(3'b000), .in5(3'b000), .in6(3'b000),
    .in7(3'b000), .out(vec), .sel(3'b000));  // open: en
endmodule

module cell_drawer (
  input  [7:0] cell_data,
  input  clk,
  output [6:0] row_0,
  output [6:0] row_1,
  output [6:0] row_2,
  output [6:0] row_3,
  output [6:0] row_4,
  output [6:0] row_5,
  output [6:0] row_6,
  output [6:0] row_7
);

  wire not_1_out;
  wire [1:0] and_1_out, or_1_out;
  wire [3:0] print;
  wire [6:0] not_2_out, not_3_out, not_4_out, not_5_out, not_6_out, not_7_out, not_8_out, not_9_out, row_0_t,
       row_1_t, row_2_t, row_3_t, row_4_t, row_5_t, row_6_t, row_7_t;
  wire [7:0] cell_data_t;

  // Probe on print
  Multiplexer #(.select(4), .width(7)) multiplexer_1 (
    .in0({7{1'b0}}), .in1({7{1'b0}}), .in2({7{1'b0}}), .in3({7{1'b0}}), .in4({7{1'b0}}), .in5({7{1'b0}}),
    .in6({7{1'b0}}), .in7({7{1'b0}}), .in8({7{1'b1}}), .in9({7{1'b0}}), .in10({7{1'b0}}), .in11({7{1'b0}}),
    .in12({7{1'b0}}), .in13({7{1'b0}}), .in14({7{1'b0}}), .in15({7{1'b0}}), .out(row_0_t), .sel(print),
    .en(1'b1));
  Multiplexer #(.select(4), .width(7)) multiplexer_2 (
    .in0({7{1'b0}}), .in1(7'b0111110), .in2(7'b0101010), .in3(7'b0101010), .in4(7'b0111110),
    .in5(7'b0101010), .in6(7'b0101010), .in7(7'b0101000), .in8(7'b1000001), .in9(7'b0011100),
    .in10(7'b0111000), .in11({7{1'b0}}), .in12({7{1'b0}}), .in13({7{1'b0}}), .in14({7{1'b0}}),
    .in15({7{1'b0}}), .out(row_4_t), .sel(print), .en(1'b1));
  Register register_1 (.D(cell_data), .Q(cell_data_t), .clk(clk));  // open: en, clr
  // Probe on row_0_t
  and and_1 (and_1_out[0], cell_data_t[3], cell_data_t[6]);
  not not_1 (not_1_out, cell_data_t[3]);
  and and_2 (and_1_out[1], not_1_out, cell_data_t[6]);
  Multiplexer #(.select(4), .width(7)) multiplexer_3 (
    .in0({7{1'b0}}), .in1({7{1'b0}}), .in2({7{1'b0}}), .in3({7{1'b0}}), .in4({7{1'b0}}), .in5({7{1'b0}}),
    .in6({7{1'b0}}), .in7({7{1'b0}}), .in8(7'b1000001), .in9(7'b0100010), .in10({7{1'b0}}), .in11({7{1'b0}}),
    .in12({7{1'b0}}), .in13({7{1'b0}}), .in14({7{1'b0}}), .in15({7{1'b0}}), .out(row_1_t), .sel(print),
    .en(1'b1));
  Multiplexer #(.select(4), .width(7)) multiplexer_4 (
    .in0({7{1'b0}}), .in1({7{1'b0}}), .in2(7'b0010010), .in3(7'b0010100), .in4(7'b0000100), .in5(7'b0100100),
    .in6(7'b0000100), .in7(7'b0110000), .in8(7'b1000001), .in9(7'b0001000), .in10(7'b0111000),
    .in11({7{1'b0}}), .in12({7{1'b0}}), .in13({7{1'b0}}), .in14({7{1'b0}}), .in15({7{1'b0}}), .out(row_5_t),
    .sel(print), .en(1'b1));
  assign or_1_out = and_1_out | {2{cell_data_t[4]}};  // OR_Gate or_1, 2 bits wide
  // Probe on print
  Multiplexer #(.select(2), .width(4)) multiplexer_5 (
    .in0(4'b1000), .in1(4'b1001), .in2({1'b0, cell_data_t[2:0]}), .in3(4'b1010), .out(print), .sel(or_1_out));  // open: en
  Multiplexer #(.select(4), .width(7)) multiplexer_6 (
    .in0({7{1'b0}}), .in1({7{1'b0}}), .in2(7'b0100110), .in3(7'b0100010), .in4(7'b0001100), .in5(7'b0111010),
    .in6(7'b0011100), .in7(7'b0100000), .in8(7'b1000001), .in9(7'b0001000), .in10(7'b0111110),
    .in11({7{1'b0}}), .in12({7{1'b0}}), .in13({7{1'b0}}), .in14({7{1'b0}}), .in15({7{1'b0}}), .out(row_2_t),
    .sel(print), .en(1'b1));
  Multiplexer #(.select(4), .width(7)) multiplexer_7 (
    .in0({7{1'b0}}), .in1({7{1'b0}}), .in2({7{1'b0}}), .in3({7{1'b0}}), .in4({7{1'b0}}), .in5({7{1'b0}}),
    .in6({7{1'b0}}), .in7({7{1'b0}}), .in8(7'b1000001), .in9(7'b0100010), .in10({7{1'b0}}), .in11({7{1'b0}}),
    .in12({7{1'b0}}), .in13({7{1'b0}}), .in14({7{1'b0}}), .in15({7{1'b0}}), .out(row_6_t), .sel(print),
    .en(1'b1));
  Multiplexer #(.width(7)) multiplexer_8 (.in0(row_0_t), .in1(not_2_out), .out(row_0), .sel(cell_data_t[5]), .en(1'b1));
  assign not_2_out = ~row_0_t;  // NOT_Gate not_2, 7 bits wide
  Multiplexer #(.width(7)) multiplexer_9 (.in0(row_1_t), .in1(not_3_out), .out(row_1), .sel(cell_data_t[5]), .en(1'b1));
  assign not_3_out = ~row_1_t;  // NOT_Gate not_3, 7 bits wide
  Multiplexer #(.width(7)) multiplexer_10 (
    .in0(row_2_t), .in1(not_4_out), .out(row_2), .sel(cell_data_t[5]), .en(1'b1));
  assign not_4_out = ~row_2_t;  // NOT_Gate not_4, 7 bits wide
  Multiplexer #(.width(7)) multiplexer_11 (
    .in0(row_3_t), .in1(not_5_out), .out(row_3), .sel(cell_data_t[5]), .en(1'b1));
  assign not_5_out = ~row_3_t;  // NOT_Gate not_5, 7 bits wide
  Multiplexer #(.width(7)) multiplexer_12 (
    .in0(row_4_t), .in1(not_6_out), .out(row_4), .sel(cell_data_t[5]), .en(1'b1));
  assign not_6_out = ~row_4_t;  // NOT_Gate not_6, 7 bits wide
  Multiplexer #(.width(7)) multiplexer_13 (
    .in0(row_5_t), .in1(not_7_out), .out(row_5), .sel(cell_data_t[5]), .en(1'b1));
  assign not_7_out = ~row_5_t;  // NOT_Gate not_7, 7 bits wide
  Multiplexer #(.width(7)) multiplexer_14 (
    .in0(row_6_t), .in1(not_8_out), .out(row_6), .sel(cell_data_t[5]), .en(1'b1));
  assign not_8_out = ~row_6_t;  // NOT_Gate not_8, 7 bits wide
  Multiplexer #(.width(7)) multiplexer_15 (
    .in0(row_7_t), .in1(not_9_out), .out(row_7), .sel(cell_data_t[5]), .en(1'b1));
  assign not_9_out = ~row_7_t;  // NOT_Gate not_9, 7 bits wide
  Multiplexer #(.select(4), .width(7)) multiplexer_16 (
    .in0({7{1'b0}}), .in1(7'b0100000), .in2(7'b0101010), .in3(7'b0101010), .in4(7'b0010100),
    .in5(7'b0101010), .in6(7'b0101010), .in7(7'b0100110), .in8(7'b1000001), .in9(7'b0011100),
    .in10(7'b0111000), .in11({7{1'b0}}), .in12({7{1'b0}}), .in13({7{1'b0}}), .in14({7{1'b0}}),
    .in15({7{1'b0}}), .out(row_3_t), .sel(print), .en(1'b1));
  Multiplexer #(.select(4), .width(7)) multiplexer_17 (
    .in0({7{1'b0}}), .in1({7{1'b0}}), .in2({7{1'b0}}), .in3({7{1'b0}}), .in4({7{1'b0}}), .in5({7{1'b0}}),
    .in6({7{1'b0}}), .in7({7{1'b0}}), .in8({7{1'b1}}), .in9({7{1'b0}}), .in10({7{1'b0}}), .in11({7{1'b0}}),
    .in12({7{1'b0}}), .in13({7{1'b0}}), .in14({7{1'b0}}), .in15({7{1'b0}}), .out(row_7_t), .sel(print),
    .en(1'b1));
  DotMatrix #(.matrixcols(8)) dotmatrix_1 (
    .col0(row_0), .col1(row_1), .col2(row_2), .col3(row_3), .col4(row_4), .col5(row_5), .col6(row_6),
    .col7(row_7));

  // Other names for the same wires on the sheet: selected = cell_data_t[5]
endmodule

module row_drawer (
  input  clk,
  input  left,
  input  right,
  input  [31:0] data,
  output [6:0] _00,
  output [6:0] _40,
  output [6:0] _01,
  output [6:0] _41,
  output [6:0] _02,
  output [6:0] _42,
  output [6:0] _03,
  output [6:0] _43,
  output [6:0] _04,
  output [6:0] _44,
  output [6:0] _05,
  output [6:0] _45,
  output [6:0] _06,
  output [6:0] _46,
  output [6:0] _07,
  output [6:0] _47,
  output [6:0] _10,
  output [6:0] _50,
  output [6:0] _11,
  output [6:0] _51,
  output [6:0] _12,
  output [6:0] _52,
  output [6:0] _13,
  output [6:0] _53,
  output [6:0] _14,
  output [6:0] _54,
  output [6:0] _15,
  output [6:0] _55,
  output [6:0] _16,
  output [6:0] _56,
  output [6:0] _17,
  output [6:0] _57,
  output [6:0] _20,
  output [6:0] _60,
  output [6:0] _21,
  output [6:0] _61,
  output [6:0] _22,
  output [6:0] _62,
  output [6:0] _23,
  output [6:0] _63,
  output [6:0] _24,
  output [6:0] _64,
  output [6:0] _25,
  output [6:0] _65,
  output [6:0] _26,
  output [6:0] _66,
  output [6:0] _27,
  output [6:0] _67,
  output [6:0] _30,
  output [6:0] _70,
  output [6:0] _31,
  output [6:0] _71,
  output [6:0] _32,
  output [6:0] _72,
  output [6:0] _33,
  output [6:0] _73,
  output [6:0] _34,
  output [6:0] _74,
  output [6:0] _35,
  output [6:0] _75,
  output [6:0] _36,
  output [6:0] _76,
  output [6:0] _37,
  output [6:0] _77
);

  wire and_1_out, and_2_out;

  and and_1 (and_1_out, left, clk);
  cell_drawer cell_drawer_1 (
    .cell_data(data[7:0]), .clk(and_1_out), .row_0(_00), .row_1(_01), .row_2(_02), .row_3(_03), .row_4(_04),
    .row_5(_05), .row_6(_06), .row_7(_07));
  cell_drawer cell_drawer_2 (
    .cell_data(data[15:8]), .clk(and_1_out), .row_0(_10), .row_1(_11), .row_2(_12), .row_3(_13), .row_4(_14),
    .row_5(_15), .row_6(_16), .row_7(_17));
  cell_drawer cell_drawer_3 (
    .cell_data(data[23:16]), .clk(and_1_out), .row_0(_20), .row_1(_21), .row_2(_22), .row_3(_23),
    .row_4(_24), .row_5(_25), .row_6(_26), .row_7(_27));
  cell_drawer cell_drawer_4 (
    .cell_data(data[31:24]), .clk(and_1_out), .row_0(_30), .row_1(_31), .row_2(_32), .row_3(_33),
    .row_4(_34), .row_5(_35), .row_6(_36), .row_7(_37));
  and and_2 (and_2_out, clk, right);
  cell_drawer cell_drawer_5 (
    .cell_data(data[7:0]), .clk(and_2_out), .row_0(_40), .row_1(_41), .row_2(_42), .row_3(_43), .row_4(_44),
    .row_5(_45), .row_6(_46), .row_7(_47));
  cell_drawer cell_drawer_6 (
    .cell_data(data[15:8]), .clk(and_2_out), .row_0(_50), .row_1(_51), .row_2(_52), .row_3(_53), .row_4(_54),
    .row_5(_55), .row_6(_56), .row_7(_57));
  cell_drawer cell_drawer_7 (
    .cell_data(data[23:16]), .clk(and_2_out), .row_0(_60), .row_1(_61), .row_2(_62), .row_3(_63),
    .row_4(_64), .row_5(_65), .row_6(_66), .row_7(_67));
  cell_drawer cell_drawer_8 (
    .cell_data(data[31:24]), .clk(and_2_out), .row_0(_70), .row_1(_71), .row_2(_72), .row_3(_73),
    .row_4(_74), .row_5(_75), .row_6(_76), .row_7(_77));
endmodule

module video_handler (
  input  [31:0] row_part,
  input  clk,
  input  [3:0] row_num,
  output [31:0] data,
  output clk_0,
  output clk_1,
  output clk_2,
  output clk_3,
  output clk_4,
  output clk_5,
  output clk_6,
  output clk_7,
  output left_clk,
  output right_clk
);

  wire [3:0] divider_2_out, divider_2_rem;

  Divider #(.width(4)) divider_1 (.a(4'b1000), .b(row_num));  // open: out, upper, rem
  Demultiplexer demultiplexer_1 (.out0(left_clk), .out1(right_clk), .in(1'b1), .sel(divider_2_rem[0]));  // open: en
  Demultiplexer #(.select(3)) demultiplexer_2 (
    .out0(clk_0), .out1(clk_1), .out2(clk_2), .out3(clk_3), .out4(clk_4), .out5(clk_5), .out6(clk_6),
    .out7(clk_7), .in(clk), .sel(divider_2_out[2:0]));  // open: en
  Divider #(.width(4)) divider_2 (.a(row_num), .b(4'b0010), .out(divider_2_out), .rem(divider_2_rem));  // open: upper

  assign data = row_part;
endmodule

module map_loader (
  input  clk,
  input  reset,
  output loaded,
  output [7:0] data,
  output [7:0] addr
);

  wire and_1_out, and_2_out, and_3_out, not_1_out, not_2_out, not_3_out, or_1_out, t_ff_1_q, t_ff_2_q;

  and and_1 (and_1_out, t_ff_2_q, ~t_ff_1_q);  // AND_Gate
  T_Flip_Flop t_ff_1 (.clk(and_1_out), .T(and_1_out), .Q(t_ff_1_q), .reset(not_1_out));  // open: Qn, preset, en
  not not_1 (not_1_out, reset);
  or or_1 (or_1_out, and_1_out, and_2_out);
  and and_2 (and_2_out, ~loaded, clk);  // AND_Gate
  and and_3 (and_3_out, reset, ~t_ff_2_q);  // AND_Gate
  Counter counter_1 (.load(reset), .D({8{1'b1}}), .Q(addr), .clk(or_1_out), .clr(and_3_out));  // open: count, carry
  T_Flip_Flop t_ff_2 (.clk(and_3_out), .T(and_3_out), .Q(t_ff_2_q), .reset(not_2_out));  // open: Qn, preset, en
  Comparator comparator_1 (.a(addr), .b(8'h40), .eq(loaded));  // open: gt, lt
  not not_2 (not_2_out, reset);
  map_selector map_selector_1 (.addr(addr), .sel(not_3_out), .clk(reset), .cell_info(data));
  Pull_Resistor pull_resistor_1 (.node(data));
  not not_3 (not_3_out, loaded);
endmodule

module delayer (
  input  bus_0,
  output first,
  output second
);

  wire not_1_out;

  and and_1 (first, ~second, bus_0);  // AND_Gate
  not not_1 (not_1_out, bus_0);
  T_Flip_Flop t_ff_1 (.clk(first), .T(first), .Q(second), .reset(not_1_out));  // open: Qn, preset, en
endmodule
